// Logisim project control_logic.circ as structural Verilog: 1 circuit, main circuit control_logic
module control_logic (
  input  [31:0] inst,
  input  BrEq,
  input  BrLt,
  output PCSel,
  output RegWEn,
  output [2:0] ImmSel,
  output BrUn,
  output ASel,
  output BSel,
  output [3:0] ALUSel,
  output MemRW,
  output [1:0] WBSel
);

  wire and_6_out, not_1_out, not_2_out, not_3_out, not_4_out, not_5_out, not_6_out, not_7_out;

  Multiplexer #(.select(5), .width(4), .enable("false")) multiplexer_1 (
    .in0(4'b0000), .in1(4'b0110), .in3(4'b0111), .in4(4'b0011), .in5(4'b0100), .in6(4'b0010), .in7(4'b0001),
    .in8(4'b1010), .in9(4'b1110), .in11(4'b1011), .in13(4'b1000), .in15(4'b1001), .in16(4'b1100),
    .in21(4'b0101), .out(ALUSel), .sel({inst[30], inst[25], inst[14:12]}));  // open: in2, in10, in12, in14, in17, in18, in19, in20, in22, in23, in24, in25, in26, in27, in28, in29, in30, in31
  not not_1 (not_1_out, inst[2]);
  not not_2 (not_2_out, inst[3]);
  not not_3 (not_3_out, inst[4]);
  not not_4 (not_4_out, inst[6]);
  Multiplexer #(.enable("false")) multiplexer_2 (.in0(BrEq), .in1(BrLt), .out(PCSel), .sel(inst[14]));
  not not_5 (not_5_out, inst[31]);
  not not_6 (not_6_out, inst[6]);
  not not_7 (not_7_out, inst[3]);
  and and_1 (BrUn, inst[13], inst[14]);
  and and_2 (RegWEn, inst[29], not_5_out);
  and and_3 (ImmSel[0], inst[4], not_6_out, inst[3]);
  and and_4 (ImmSel[1], inst[5], inst[2]);
  and and_5 (ASel, inst[0], inst[1], inst[2], inst[5]);
  and and_6 (and_6_out, inst[0], inst[1], not_7_out);
  and and_7 (MemRW, inst[0], inst[1], not_1_out, not_2_out, not_3_out, inst[5], not_4_out);
  or or_1 (BSel, ASel, and_6_out);

  assign ImmSel[2] = inst[3];

  // Other names for the same wires on the sheet: func3[2:0] = inst[14:12]; func7[6:0] = inst[31:25];
  //   opcode[6:0] = inst[6:0]

  // Notes on the sheet:
  //   INPUTS to your circuit
  //   DON'T CHANGE THE LOCATIONS OF THE INPUTS AND OUTPUTS!
  //   OUTPUT from your circuit
endmodule
